# Fritzing sketch raspberrypi (saved by Fritzing 0.9.3b)
breadboards: 1

parts:
  Raspberry_Pi_1 = Raspberry Pi 3 [part_number=RPI-3-V1.2]
  R1 = Resistor [tolerance=±5% resistance=220 package=THT]
  LED1 = LED - 5mm [color="Red (633nm)" package="5 mm [THT]"]
  LED2 = LED - 5mm [color="Yellow (595nm)" package="5 mm [THT]"]
  R2 = Resistor [tolerance=±5% resistance=220 package=THT]
  LED3 = LED - 5mm [color="Green (555nm)" package="5 mm [THT]"]
  R3 = Resistor [tolerance=±5% resistance=220 package=THT]

nets:
  N1: Raspberry_Pi_1.GIPO4, R1.Pin_1
  N2: Raspberry_Pi_1.GND, LED1.cathode, LED2.cathode, LED3.cathode
  N3: Raspberry_Pi_1.GIPO17, R2.Pin_1
  N4: Raspberry_Pi_1.GIPO27, R3.Pin_1
  N5: R1.Pin_0, LED1.anode
  N6: LED2.anode, R2.Pin_0
  N7: LED3.anode, R3.Pin_0
